// Logisim project Computer-16.circ as structural Verilog: 3 circuits, main circuit main
module main (
);

  wire ACCIn, AccToBus, and_1_out, and_2_out, and_3_out, and_4_out, and_5_out, AToBus, BToBus, BusToA,
       BusToB, BusToC, BusToFl, BusToM, BusToMAR, BusToN, CLK, clock_1_out, CToBus, FlToBus, HLT, HLTF,
       IMMEM, IMMNW, IMMToBus, IMMVN, IMRST, JE, JMP, JMPADDR, JMPADDRCOMP, JNE, LDADDR, LogToBus, MEMWR,
       MEMWRN, not_1_out, not_2_out, not_3_out, not_4_out, not_5_out, not_6_out, not_7_out, NToBus, or_2_out,
       or_3_out, pull_resistor_12_node, SWMEM;
  wire [2:0] ALUFLAGS, LOGICFLAGS;
  wire [3:0] ALUOUTFLAGS;
  wire [4:0] pull_resistor_5_node, pull_resistor_9_node;
  wire [7:0] pull_resistor_22_node, pull_resistor_22_node_2, undriven, undriven_2;
  wire [14:0] multiplier_1_out, multiplier_2_out, pull_resistor_17_node;
  wire [15:0] ACCData, ADDRB, bit_extender_1_out, CALCREG, CBUS, controlled_buffer_6_out, DATAB, FLAGSAL,
       LOGICBS, MARB;
  wire [15:4] SYSFLAGS;

  Clock clock_1 (.out(clock_1_out));
  Pull_Resistor pull_resistor_1 (.node(DATAB));
  Pull_Resistor pull_resistor_2 (.node(ADDRB));
  Pull_Resistor pull_resistor_3 (.node(FLAGSAL));
  assign CLK = HLTF ? clock_1_out : 1'bz;  // Controlled_Buffer controlled_buffer_1
  // LedBar #(.inputtype("row"), .matrixcols(16)) ledbar_1: pin names not known; wires that end beside it: DATAB
  // LedBar #(.inputtype("row"), .matrixcols(16)) ledbar_2: pin names not known; wires that end beside it: ADDRB
  // LedBar #(.inputtype("row"), .matrixcols(16)) ledbar_3: pin names not known; wires that end beside it: FLAGSAL
  Pull_Resistor pull_resistor_4 (.node(CLK));
  or or_1 (ACCIn, ALUFLAGS[0], ALUFLAGS[1], ALUFLAGS[2]);
  Pull_Resistor pull_resistor_5 (.node(pull_resistor_5_node));
  Pull_Resistor pull_resistor_6 (.node(ALUFLAGS));
  Pull_Resistor pull_resistor_7 (.node(SYSFLAGS));
  Pull_Resistor pull_resistor_8 (.node(IMMEM));
  alu alu_1 (
    .TwoIn(CALCREG), .OneIn(DATAB), .Selector(ALUFLAGS), .LogicOut(LOGICFLAGS), .ValOut(ACCData),
    .Flags(ALUOUTFLAGS));
  Demultiplexer #(.select(5)) demultiplexer_1 (
    .out1(BusToA), .out2(BusToM), .out3(BusToB), .out4(BusToN), .out5(BusToFl), .out6(LDADDR),
    .out7(BusToMAR), .out8(BusToC), .out30(JNE), .out31(JE), .in(1'b1), .sel(pull_resistor_5_node));  // open: out0, out9, out10, out11, out12, out13, out14, out15, out16, out17, out18, out19, out20, out21, out22, out23, out24, out25, out26, out27, out28, out29
  regstr LOGIC_FLAGS (
    .DataIn(bit_extender_1_out), .CTRLIn(ACCIn), .CLCK(CLK), .CTRLOut(1'b1), .DataOut(LOGICBS));  // open: RST
  Bit_Extender #(.in_width(3), .\type ("input")) bit_extender_1 (
    .in(LOGICFLAGS), .out(bit_extender_1_out));  // open: extend
  assign DATAB = LogToBus ? LOGICBS : 16'bz;  // Controlled_Buffer controlled_buffer_2
  not not_1 (not_1_out, LOGICBS[1]);
  Pull_Resistor pull_resistor_9 (.node(pull_resistor_9_node));
  and and_1 (and_1_out, JE, LOGICBS[1]);
  and and_2 (and_2_out, JNE, not_1_out);
  assign pull_resistor_9_node = not_2_out ? pull_resistor_17_node[6:2] : 5'bz;  // Controlled_Buffer controlled_buffer_3
  assign pull_resistor_5_node = not_2_out ? pull_resistor_17_node[11:7] : 5'bz;  // Controlled_Buffer controlled_buffer_4
  assign ALUFLAGS = not_2_out ? pull_resistor_17_node[14:12] : 3'bz;  // Controlled_Buffer controlled_buffer_5
  or or_2 (or_2_out, ACCIn, BusToFl);
  Pull_Resistor pull_resistor_10 ();  // open: node
  Transistor transistor_1 (.in(and_1_out), .out(JMP), .gate(1'b0));
  Pull_Resistor pull_resistor_11 (.node(JMP));
  Transistor transistor_2 (.in(and_2_out), .out(JMP), .gate(1'b0));
  Demultiplexer #(.select(5)) demultiplexer_2 (
    .out1(AToBus), .out2(BToBus), .out3(NToBus), .out4(AccToBus), .out5(FlToBus), .out6(IMMToBus),
    .out7(CToBus), .out8(LogToBus), .out31(HLT), .in(1'b1), .sel(pull_resistor_9_node));  // open: out0, out9, out10, out11, out12, out13, out14, out15, out16, out17, out18, out19, out20, out21, out22, out23, out24, out25, out26, out27, out28, out29, out30
  not not_2 (not_2_out, pull_resistor_12_node);
  Pull_Resistor pull_resistor_12 (.node(pull_resistor_12_node));
  assign controlled_buffer_6_out = ACCIn ? {SYSFLAGS, ALUOUTFLAGS} : 16'bz;  // Controlled_Buffer controlled_buffer_6
  Pull_Resistor pull_resistor_13 (.node(ACCIn));
  assign controlled_buffer_6_out = FlToBus ? DATAB : 16'bz;  // Controlled_Buffer controlled_buffer_7
  regstr FLAGS (
    .DataIn(controlled_buffer_6_out), .CTRLIn(or_2_out), .CLCK(CLK), .CTRLOut(FlToBus), .DataOut(DATAB));  // open: RST
  assign pull_resistor_12_node = not_3_out ? IMMVN : 1'bz;  // Controlled_Buffer controlled_buffer_8
  not not_3 (not_3_out, IMMNW);
  regstr MAR (.DataIn(DATAB), .CTRLIn(BusToMAR), .CLCK(CLK), .CTRLOut(1'b1), .DataOut(MARB));  // open: RST
  Pull_Resistor pull_resistor_14 (.node(MEMWR));
  assign MEMWR = pull_resistor_17_node[1] ? 1'b1 : 1'bz;  // Controlled_Buffer controlled_buffer_9
  regstr NUMBR (.DataIn(DATAB), .CTRLIn(BusToN), .CLCK(CLK), .CTRLOut(1'b1), .DataOut(CALCREG));  // open: RST
  T_Flip_Flop #(.trigger("falling")) MEMWR_FLAG (.T(MEMWR), .clk(CLK), .Q(MEMWRN));  // open: Qn, reset, preset
  T_Flip_Flop #(.trigger("falling")) MEMRE_FLAG (
    .T(IMMEM), .clk(CLK), .Q(JMPADDR), .Qn(JMPADDRCOMP));  // open: reset, preset
  regstr ACC (.DataIn(ACCData), .CTRLIn(ACCIn), .CLCK(CLK), .CTRLOut(AccToBus), .DataOut(DATAB));  // open: RST
  assign DATAB = NToBus ? CALCREG : 16'bz;  // Controlled_Buffer controlled_buffer_10
  Pull_Resistor pull_resistor_15 (.node(NToBus));
  T_Flip_Flop #(.trigger("falling")) u_HLT (.T(HLT), .clk(CLK), .Qn(HLTF));  // open: Q, reset, preset
  Pull_Resistor pull_resistor_16 (.node(IMMVN));
  assign IMMVN = pull_resistor_17_node[0] ? 1'b1 : 1'bz;  // Controlled_Buffer controlled_buffer_11
  Pull_Resistor pull_resistor_17 (.node({IMMEM, pull_resistor_17_node}));
  assign {IMMEM, pull_resistor_17_node} = CLK ? CBUS : 16'bz;  // Controlled_Buffer controlled_buffer_12
  Pull_Resistor pull_resistor_18 (.node(CBUS));
  regstr REGSTRA (.DataIn(DATAB), .CTRLIn(BusToA), .CLCK(CLK), .CTRLOut(AToBus), .DataOut(DATAB));  // open: RST
  regstr CBUS_CACHE (.DataIn(CBUS), .CTRLIn(IMMVN), .CLCK(CLK), .CTRLOut(IMMNW), .DataOut(CBUS));  // open: RST
  T_Flip_Flop #(.trigger("falling")) IMMFLAG (.T(IMMVN), .clk(CLK), .Q(IMMNW), .reset(IMRST));  // open: Qn, preset
  Pull_Resistor pull_resistor_19 (.node(IMRST));
  Transistor transistor_3 (.in(IMMNW), .out(SWMEM), .gate(1'b0));
  Pull_Resistor pull_resistor_20 (.node(SWMEM));
  or or_3 (or_3_out, JMP, LDADDR);
  Counter #(.max('hffff), .trigger("falling"), .width(16)) counter_1 (
    .load(or_3_out), .up(1'b1), .count(JMPADDRCOMP), .clk(CLK), .D(DATAB), .Q(ADDRB));  // open: clr, carry
  regstr REGSTRB (.DataIn(DATAB), .CTRLIn(BusToB), .CLCK(CLK), .CTRLOut(BToBus), .DataOut(DATAB));  // open: RST
  regstr REGSTRC (.DataIn(DATAB), .CTRLIn(BusToC), .CLCK(CLK), .CTRLOut(CToBus), .DataOut(DATAB));  // open: RST
  Pull_Resistor pull_resistor_21 (.node(ADDRB));
  and and_3 (and_3_out, MEMWR, MEMWRN);
  Multiplier #(.width(15)) multiplier_1 (.a(15'h2), .b(MARB[14:0]), .out(multiplier_1_out));  // open: cin, cout
  Multiplier #(.width(15)) multiplier_2 (.a(15'h2), .b(ADDRB[14:0]), .out(multiplier_2_out));  // open: cin, cout
  // RAM #(.addrWidth(15), .enables("line"), .line("dual"), .trigger("falling")) DUAL_PORT_RAM: pin names not known; wires that end beside it: multiplier_1_out, and_3_out, 1'b1, 1'b1, CLK, DATAB[15:8], DATAB[7:0]
  // ROM #(.addrWidth(15), .line("dual")) DUAL_PORT_ROM: pin names not known; wires that end beside it: multiplier_2_out
  Pull_Resistor pull_resistor_22 (.node({pull_resistor_22_node_2, pull_resistor_22_node}));
  not not_4 (not_4_out, BusToM);
  assign CBUS = not_5_out ? {pull_resistor_22_node_2, pull_resistor_22_node} : 16'bz;  // Controlled_Buffer controlled_buffer_13
  not not_5 (not_5_out, SWMEM);
  Pull_Resistor pull_resistor_23 (.node({pull_resistor_22_node_2, pull_resistor_22_node}));
  not not_6 (not_6_out, BusToM);
  not not_7 (not_7_out, JMPADDR);
  assign DATAB = and_4_out ? {undriven_2, undriven} : 16'bz;  // Controlled_Buffer controlled_buffer_14
  and and_4 (and_4_out, JMPADDR, not_4_out);
  assign DATAB = and_5_out ? {pull_resistor_22_node_2, pull_resistor_22_node} : 16'bz;  // Controlled_Buffer controlled_buffer_15
  and and_5 (and_5_out, SWMEM, not_6_out, not_7_out);

  // Other names for the same wires on the sheet: IMMST = IMMNW; SYSFLAGS[3:0] = ALUOUTFLAGS; SYSFLAGSSET = ACCIn

  // Notes on the sheet:
  //   contents of DUAL_PORT_ROM (hex, n*v repeats v):
  //   0 81 0 7c 3 81 0 ff 81 7 2 1 0 2 30 1 0 1 f 81 0 0 0 81 0 12 1 81 0 15 2 4 10 8 4 10 2 1 0 27 30 1c
  //   f 1 0 0 0 7c
endmodule

module regstr (
  input  [15:0] DataIn,
  input  CTRLIn,
  input  CLCK,
  input  RST,
  input  CTRLOut,
  output [15:0] DataOut
);

  wire [15:0] REGSTR_q;

  Register #(.trigger("falling"), .width(16)) REGSTR (.D(DataIn), .en(CTRLIn), .clk(CLCK), .Q(REGSTR_q), .clr(RST));
  assign DataOut = CTRLOut ? REGSTR_q : 16'bz;  // Controlled_Buffer controlled_buffer_1
  Pull_Resistor pull_resistor_1 (.node(CTRLOut));
endmodule

module alu (
  input  [15:0] OneIn,
  input  [15:0] TwoIn,
  input  [2:0] Selector,
  output [15:0] ValOut,
  output [3:0] Flags,
  output [2:0] LogicOut
);

  wire [15:0] ADD1, ADD2, adder_1_out, AND1, AND2, and_1_out, COMP1, COMP2, OR1, OR2, or_1_out, SUB1, SUB2,
       subtractor_1_out, XOR1, XOR2, xor_1_out;

  Demultiplexer #(.select(3), .width(16)) demultiplexer_1 (
    .out1(ADD1), .out2(SUB1), .out3(COMP1), .out4(AND1), .out5(OR1), .out6(XOR1), .in(OneIn), .sel(Selector));  // open: out0, out7
  Demultiplexer #(.select(3), .width(16)) demultiplexer_2 (
    .out1(ADD2), .out2(SUB2), .out3(COMP2), .out4(AND2), .out5(OR2), .out6(XOR2), .in(TwoIn), .sel(Selector));  // open: out0, out7
  Comparator #(.width(16)) comparator_1 (.a(COMP1), .b(COMP2), .gt(LogicOut[0]), .eq(LogicOut[1]), .lt(LogicOut[2]));
  Adder #(.width(16)) adder_1 (.a(ADD1), .b(ADD2), .out(adder_1_out), .cout(Flags[0]));  // open: cin
  Subtractor #(.width(16)) subtractor_1 (.a(SUB1), .b(SUB2), .out(subtractor_1_out), .bout(Flags[1]));  // open: bin
  assign and_1_out = AND1 & AND2;  // AND_Gate and_1, 16 bits wide
  assign or_1_out = OR1 | OR2;  // OR_Gate or_1, 16 bits wide
  assign xor_1_out = XOR1 ^ XOR2;  // XOR_Gate xor_1, 16 bits wide
  Pull_Resistor pull_resistor_1 (.node(Flags[2]));
  Pull_Resistor pull_resistor_2 (.node(Flags[3]));
  Multiplexer #(.select(3), .width(16)) multiplexer_1 (
    .in1(adder_1_out), .in2(subtractor_1_out), .in4(and_1_out), .in5(or_1_out), .in6(xor_1_out),
    .out(ValOut), .sel(Selector));  // open: in0, in3, in7

  // Other names for the same wires on the sheet: OFLOW = Flags[0]; BORRW = Flags[1]
endmodule
